# Fritzing sketch scheme (saved by Fritzing 0.9.3b)
breadboards: 1

parts:
  Часть1 = Arduino Nano (Rev3.0)
  DFRobot_DFPlayer_Mini1 = DFRobot DFPlayer Mini [part_number=DFR0299]  # not connected
  A6_Module_Ver4 = IC, DIP package, 24 pins [chip_label="A6 GSM"]  # not connected
  2_Channel_Relay1 = 2 Channel Power Relay  # not connected
  Часть2 = LCD1602-I2C
  DS1 = DS18B20 1-Wire Temperature Sensor [part_number=DS18B20]  # not connected
  DS2 = DS18B20 1-Wire Temperature Sensor [part_number=DS18B20]  # not connected
  Power_plug2 = Power plug  # not connected
  U3 = ENCODER_RGB_CA [package=encoder_led_3]  # not connected

nets:
  N1: Часть1.A5, Часть2.SCL
  N2: Часть1.A4, Часть2.SDA

custom parts:
  2 Channel Power Relay: A 2 channel power relay. The module operates at 5V.
  LCD1602-I2C: A standard character display, usually with 2x16 characters. Comes in many colors with LCM1602 IIC attached.
